# Fritzing sketch MIDi_To_Fan_layout (saved by Fritzing 0.6.3b)
breadboards: 1

parts:
  Arduino1 = Arduino
  MIDI-_Input = DIN-5 jack (MIDI) [package=THT]
  R1 = Resistor [tolerance=±5% resistance=220 package=THT]
  D1 = Rectifier Diode [part_number=1N4001 package="300 mil [THT]"]
  R2 = Resistor [tolerance=±5% resistance=270 package=THT]
  Optocoppler = IC, DIP package, 8 pins [chip_label="6N 138 " spacing=300mil]
  Q2 = PNP-Transistor [package="TO92 [THT]"]
  Q1 = PNP-Transistor [package="TO92 [THT]"]
  SPKR1 = Loudspeaker
  VCC_for_SPKRs = Battery block 9V
  SPKR2 = Loudspeaker
  R3 = Resistor [tolerance=±5% resistance=990 package=THT]
  R4 = Resistor [tolerance=±5% resistance=990 package=THT]

nets:
  GND: Arduino1.GND, Optocoppler.pin5, Optocoppler.pin7, Q2.C, Q1.C, VCC_for_SPKRs.-
  N1: Arduino1.D8, R4.Pin_1
  N2: Arduino1.D4, R3.Pin_1
  N3: Arduino1.D0RX, R2.Pin_1, Optocoppler.pin6
  N4: MIDI-_Input.5, D1.cathode, Optocoppler.pin2
  N5: MIDI-_Input.4, R1.Pin_1
  N6: R1.Pin_0, D1.anode, Optocoppler.pin3
  N7: R2.Pin_0, Optocoppler.pin8
  N8: Q2.E, SPKR1.pin1
  N9: Q2.B, R4.Pin_0
  N10: Q1.E, SPKR2.pin1
  N11: Q1.B, R3.Pin_0
  N12: SPKR1.pin2, VCC_for_SPKRs.+, SPKR2.pin2
